// Logisim project proj_sub_2_final.circ as structural Verilog: 1 circuit, main circuit main
module main (
  input  [15:0] in_1,
  input  in_2,
  input  [7:0] in_3,
  input  in_4,
  input  in_5,
  output Done,
  output [15:0] out_7
);

  wire and_1_out, and_2_out, and_3_out, and_4_out, and_5_out, and_6_out, and_7_out, and_8_out, and_9_out,
       and_10_out, and_11_out, and_12_out, and_13_out, and_14_out, and_15_out, and_16_out, and_17_out,
       counter_1_carry, multiplexer_1_out, multiplexer_2_out, multiplexer_3_out, multiplexer_4_out,
       multiplexer_5_out, multiplexer_6_out, multiplexer_7_out, multiplexer_9_out, multiplexer_10_out,
       multiplexer_11_out, multiplexer_12_out, multiplexer_13_out, multiplexer_14_out, multiplexer_15_out,
       multiplexer_16_out, multiplexer_17_out, multiplexer_18_out, not_1_out, not_2_out, not_3_out,
       not_4_out, not_5_out, not_6_out, not_7_out, not_8_out, not_9_out, not_10_out, not_11_out, not_12_out,
       not_13_out, not_14_out, not_15_out, not_16_out, not_17_out, not_18_out, not_19_out, not_20_out,
       not_21_out, not_22_out, not_23_out, or_1_out, or_2_out, or_3_out, or_4_out, or_5_out, or_6_out,
       or_7_out, or_8_out, or_9_out, or_10_out, or_11_out, or_12_out, or_13_out, or_14_out, or_15_out,
       or_16_out, or_17_out, or_18_out, shift_register_1_out, undriven, undriven_2, undriven_3, undriven_4;
  wire [15:0] adder_1_out, d_ff_17_q, multiplexer_8_out;

  Multiplexer multiplexer_1 (.in0(in_1[15]), .in1(d_ff_17_q[14]), .out(multiplexer_1_out), .sel(not_23_out));
  D_Flip_Flop d_ff_1 (.D(multiplexer_1_out), .clk(in_2), .Q(d_ff_17_q[15]));  // open: Qn, preset, reset
  Counter #(.max('h8), .width(4)) counter_1 (
    .load(1'b0), .count(1'b1), .carry(counter_1_carry), .up(1'b1), .clk(in_2));  // open: D, Q, clr
  D_Flip_Flop d_ff_2 (.D(multiplexer_3_out), .clk(in_2), .Q(d_ff_17_q[14]));  // open: Qn, preset, reset
  D_Flip_Flop d_ff_3 (.D(multiplexer_2_out), .clk(in_2), .Q(Done));  // open: Qn, preset, reset
  Multiplexer multiplexer_2 (.in0(Done), .in1(counter_1_carry), .out(multiplexer_2_out), .sel(counter_1_carry));
  Multiplexer multiplexer_3 (.in0(in_1[14]), .in1(d_ff_17_q[13]), .out(multiplexer_3_out), .sel(not_23_out));
  D_Flip_Flop d_ff_4 (.D(multiplexer_4_out), .clk(in_2), .Q(d_ff_17_q[13]));  // open: Qn, preset, reset
  D_Flip_Flop d_ff_5 (.D(multiplexer_5_out), .clk(in_2), .Q(d_ff_17_q[12]));  // open: Qn, preset, reset
  Multiplexer multiplexer_4 (.in0(in_1[13]), .in1(d_ff_17_q[12]), .out(multiplexer_4_out), .sel(not_23_out));
  Register #(.width(16)) register_1 (.D(adder_1_out), .en(1'b1), .clk(in_2), .Q(out_7), .clr(in_5));
  Multiplexer multiplexer_5 (.in0(in_1[12]), .in1(d_ff_17_q[11]), .out(multiplexer_5_out), .sel(not_23_out));
  D_Flip_Flop d_ff_6 (.D(multiplexer_6_out), .clk(in_2), .Q(d_ff_17_q[11]));  // open: Qn, preset, reset
  Multiplexer multiplexer_6 (.in0(in_1[11]), .in1(d_ff_17_q[10]), .out(multiplexer_6_out), .sel(not_23_out));
  D_Flip_Flop d_ff_7 (.D(multiplexer_7_out), .clk(in_2), .Q(d_ff_17_q[10]));  // open: Qn, preset, reset
  Multiplexer multiplexer_7 (.in0(in_1[10]), .in1(d_ff_17_q[9]), .out(multiplexer_7_out), .sel(not_23_out));
  D_Flip_Flop d_ff_8 (.D(multiplexer_9_out), .clk(in_2), .Q(d_ff_17_q[9]));  // open: Qn, preset, reset
  not not_1 (not_1_out, in_5);
  Shift_Register shift_register_1 (
    .shift(not_1_out), .in(1'b0), .clk(in_2), .out(shift_register_1_out), .load(in_5), .clr(in_4),
    .d0(in_3[7]), .d1(in_3[6]), .d2(in_3[5]), .d3(in_3[4]), .d4(in_3[3]), .d5(in_3[2]), .d6(in_3[1]),
    .d7(in_3[0]));  // open: q0, q1, q2, q3, q4, q5, q6, q7
  Multiplexer #(.width(16)) multiplexer_8 (
    .in0({16{1'b0}}), .in1(d_ff_17_q), .out(multiplexer_8_out), .sel(shift_register_1_out));
  Multiplexer multiplexer_9 (.in0(in_1[9]), .in1(d_ff_17_q[8]), .out(multiplexer_9_out), .sel(not_23_out));
  D_Flip_Flop d_ff_9 (.D(multiplexer_10_out), .clk(in_2), .Q(d_ff_17_q[8]));  // open: Qn, preset, reset
  Adder #(.width(16)) adder_1 (.a(multiplexer_8_out), .b(out_7), .out(adder_1_out));  // open: cin, cout
  Multiplexer multiplexer_10 (.in0(in_1[8]), .in1(d_ff_17_q[7]), .out(multiplexer_10_out), .sel(not_23_out));
  D_Flip_Flop d_ff_10 (.D(multiplexer_11_out), .clk(in_2), .Q(d_ff_17_q[7]));  // open: Qn, preset, reset
  Multiplexer multiplexer_11 (.in0(in_1[7]), .in1(d_ff_17_q[6]), .out(multiplexer_11_out), .sel(not_23_out));
  D_Flip_Flop d_ff_11 (.D(multiplexer_12_out), .clk(in_2), .Q(d_ff_17_q[6]));  // open: Qn, preset, reset
  Multiplexer multiplexer_12 (.in0(in_1[6]), .in1(d_ff_17_q[5]), .out(multiplexer_12_out), .sel(not_23_out));
  D_Flip_Flop d_ff_12 (.D(multiplexer_13_out), .clk(in_2), .Q(d_ff_17_q[5]));  // open: Qn, preset, reset
  Multiplexer multiplexer_13 (.in0(in_1[5]), .in1(d_ff_17_q[4]), .out(multiplexer_13_out), .sel(not_23_out));
  D_Flip_Flop d_ff_13 (.D(multiplexer_14_out), .clk(in_2), .Q(d_ff_17_q[4]));  // open: Qn, preset, reset
  not not_2 (not_2_out, undriven_2);
  not not_3 (not_3_out, undriven_3);
  not not_4 (not_4_out, undriven);
  not not_5 (not_5_out, undriven_3);
  not not_6 (not_6_out, undriven);
  not not_7 (not_7_out, undriven_2);
  not not_8 (not_8_out, undriven_3);
  not not_9 (not_9_out, undriven_2);
  not not_10 (not_10_out, undriven);
  not not_11 (not_11_out, undriven_2);
  not not_12 (not_12_out, undriven_3);
  not not_13 (not_13_out, undriven_3);
  not not_14 (not_14_out, undriven);
  not not_15 (not_15_out, undriven_3);
  not not_16 (not_16_out, undriven);
  not not_17 (not_17_out, undriven_3);
  not not_18 (not_18_out, undriven_2);
  not not_19 (not_19_out, undriven);
  not not_20 (not_20_out, undriven_3);
  Multiplexer multiplexer_14 (.in0(in_1[4]), .in1(d_ff_17_q[3]), .out(multiplexer_14_out), .sel(not_23_out));
  D_Flip_Flop d_ff_14 (.D(multiplexer_15_out), .clk(in_2), .Q(d_ff_17_q[3]));  // open: Qn, preset, reset
  and and_1 (and_1_out, not_2_out, not_3_out);
  and and_2 (and_2_out, undriven_2, undriven_3);
  not not_21 (not_21_out, undriven_2);
  and and_3 (and_3_out, not_4_out, not_5_out);
  or or_1 (or_1_out, not_6_out, undriven_3);
  and and_4 (and_4_out, not_7_out, not_8_out);
  and and_5 (and_5_out, not_9_out, undriven);
  not not_22 (not_22_out, undriven_3);
  and and_6 (and_6_out, undriven_2, not_10_out);
  and and_7 (and_7_out, not_11_out, not_12_out);
  and and_8 (and_8_out, undriven, not_13_out);
  and and_9 (and_9_out, not_14_out, not_15_out);
  and and_10 (and_10_out, undriven_2, not_16_out);
  and and_11 (and_11_out, undriven_2, not_17_out);
  and and_12 (and_12_out, not_18_out, undriven);
  and and_13 (and_13_out, undriven_2, not_19_out);
  and and_14 (and_14_out, undriven_2, not_20_out);
  Multiplexer multiplexer_15 (.in0(in_1[3]), .in1(d_ff_17_q[2]), .out(multiplexer_15_out), .sel(not_23_out));
  D_Flip_Flop d_ff_15 (.D(multiplexer_16_out), .clk(in_2), .Q(d_ff_17_q[2]));  // open: Qn, preset, reset
  or or_2 (or_2_out, and_1_out, undriven);
  or or_3 (or_3_out, and_2_out, undriven_4);
  or or_4 (or_4_out, not_21_out, and_3_out);
  and and_15 (and_15_out, undriven, undriven_3);
  or or_5 (or_5_out, or_1_out, undriven_2);
  or or_6 (or_6_out, and_4_out, and_5_out);
  and and_16 (and_16_out, undriven, not_22_out);
  and and_17 (and_17_out, and_6_out, undriven_3);
  or or_7 (or_7_out, and_7_out, and_8_out);
  or or_8 (or_8_out, and_9_out, and_10_out);
  or or_9 (or_9_out, and_11_out, undriven_4);
  or or_10 (or_10_out, and_12_out, and_13_out);
  or or_11 (or_11_out, and_14_out, undriven_4);
  Multiplexer multiplexer_16 (.in0(in_1[2]), .in1(d_ff_17_q[1]), .out(multiplexer_16_out), .sel(not_23_out));
  D_Flip_Flop d_ff_16 (.D(multiplexer_17_out), .clk(in_2), .Q(d_ff_17_q[1]));  // open: Qn, preset, reset
  or or_12 (or_12_out, or_2_out, or_3_out);
  or or_13 (or_13_out, or_4_out, and_15_out);
  or or_14 (or_14_out, or_6_out, and_16_out);
  or or_15 (or_15_out, or_14_out, or_16_out);
  or or_16 (or_16_out, and_17_out, undriven_4);
  or or_17 (or_17_out, or_8_out, or_9_out);
  or or_18 (or_18_out, or_10_out, or_11_out);
  Multiplexer multiplexer_17 (.in0(in_1[1]), .in1(d_ff_17_q[0]), .out(multiplexer_17_out), .sel(not_23_out));
  D_Flip_Flop d_ff_17 (.D(multiplexer_18_out), .clk(in_2), .Q(d_ff_17_q[0]));  // open: Qn, preset, reset
  _7_Segment_Display u_7_segment_display_1 (
    .g(or_18_out), .f(or_17_out), .a(or_12_out), .b(or_13_out), .e(or_7_out), .d(or_15_out), .c(or_5_out));  // open: dp
  Multiplexer multiplexer_18 (.in0(in_1[0]), .in1(1'b0), .out(multiplexer_18_out), .sel(not_23_out));
  not not_23 (not_23_out, in_5);

  // Notes on the sheet:
  //   Multipliar
  //   7-segment display (Output)
  //   Multiplicand - LSR
endmodule
