// Logisim project seg7disp.circ as structural Verilog
module _7_seg_disp (
  input  d,
  input  c,
  input  b,
  input  a
);

  wire and_1_out, and_2_out, and_3_out, and_4_out, and_5_out, and_6_out, and_7_out, and_8_out, and_9_out,
       and_10_out, and_11_out, and_12_out, and_13_out, and_14_out, and_15_out, and_16_out, and_17_out,
       not_1_out, not_2_out, not_3_out, not_4_out, not_5_out, not_6_out, not_7_out, not_8_out, not_9_out,
       not_10_out, not_11_out, not_12_out, not_13_out, not_14_out, not_15_out, not_16_out, not_17_out,
       not_18_out, not_19_out, not_20_out, not_21_out, or_1_out, or_2_out, or_3_out, or_4_out, or_5_out,
       or_6_out, or_7_out, or_8_out, or_9_out, or_10_out, or_11_out, or_12_out, or_13_out, or_14_out,
       or_15_out, or_16_out, or_17_out, or_18_out;

  not not_1 (not_1_out, c);
  and and_1 (and_1_out, not_1_out, not_2_out);
  not not_2 (not_2_out, a);
  and and_2 (and_2_out, c, a);
  not not_3 (not_3_out, c);
  not not_4 (not_4_out, b);
  and and_3 (and_3_out, not_4_out, not_5_out);
  not not_5 (not_5_out, a);
  not not_6 (not_6_out, b);
  or or_1 (or_1_out, not_6_out, a);
  not not_7 (not_7_out, c);
  and and_4 (and_4_out, not_7_out, not_8_out);
  not not_8 (not_8_out, a);
  not not_9 (not_9_out, c);
  and and_5 (and_5_out, not_9_out, b);
  not not_10 (not_10_out, a);
  and and_6 (and_6_out, c, not_11_out);
  not not_11 (not_11_out, b);
  not not_12 (not_12_out, c);
  and and_7 (and_7_out, not_12_out, not_13_out);
  not not_13 (not_13_out, a);
  and and_8 (and_8_out, b, not_14_out);
  not not_14 (not_14_out, a);
  not not_15 (not_15_out, b);
  and and_9 (and_9_out, not_15_out, not_16_out);
  not not_16 (not_16_out, a);
  and and_10 (and_10_out, c, not_17_out);
  not not_17 (not_17_out, b);
  and and_11 (and_11_out, c, not_18_out);
  not not_18 (not_18_out, a);
  not not_19 (not_19_out, c);
  and and_12 (and_12_out, not_19_out, b);
  and and_13 (and_13_out, c, not_20_out);
  not not_20 (not_20_out, b);
  and and_14 (and_14_out, c, not_21_out);
  not not_21 (not_21_out, a);
  or or_2 (or_2_out, and_1_out, b);
  or or_3 (or_3_out, and_2_out, d);
  or or_4 (or_4_out, not_3_out, and_3_out);
  and and_15 (and_15_out, b, a);
  or or_5 (or_5_out, or_1_out, c);
  or or_6 (or_6_out, and_4_out, and_5_out);
  and and_16 (and_16_out, b, not_10_out);
  and and_17 (and_17_out, and_6_out, a);
  or or_7 (or_7_out, and_7_out, and_8_out);
  or or_8 (or_8_out, and_9_out, and_10_out);
  or or_9 (or_9_out, and_11_out, d);
  or or_10 (or_10_out, and_12_out, and_13_out);
  or or_11 (or_11_out, and_14_out, d);
  or or_12 (or_12_out, or_2_out, or_3_out);
  or or_13 (or_13_out, or_4_out, and_15_out);
  or or_14 (or_14_out, or_6_out, and_16_out);
  or or_15 (or_15_out, and_17_out, d);
  or or_16 (or_16_out, or_8_out, or_9_out);
  or or_17 (or_17_out, or_10_out, or_11_out);
  or or_18 (or_18_out, or_14_out, or_15_out);
  _7_Segment_Display u_7_segment_display_1 (
    .g(or_17_out), .f(or_16_out), .a(or_12_out), .b(or_13_out), .e(or_7_out), .d(or_18_out), .c(or_5_out));  // open: dp
endmodule
